// Digital circuit S29GL064.dig as structural Verilog
// S29GL064N — 64 Mbit (4M x 16) NOR Flash
// 3.0V, 90ns, TSOP-48
// Equivalent to MX29LV640E
module S29GL064 (
  input  nCE,
  input  nOE,
  input  A_1,
  input  A0,
  input  A1,
  input  A2,
  input  A3,
  input  A4,
  input  A5,
  input  A6,
  input  A7,
  input  A8,
  input  A9,
  input  A10,
  input  A11,
  input  A12,
  input  A13,
  input  A14,
  input  A15,
  input  A16,
  input  A17,
  input  A18,
  input  VCC,
  input  GND,
  input  DQ0,
  input  DQ1,
  input  DQ2,
  input  DQ3,
  input  DQ4,
  input  DQ5,
  input  DQ6,
  input  DQ7,
  input  DQ8,
  input  DQ9,
  input  DQ10,
  input  DQ11,
  input  DQ12,
  input  DQ13,
  input  DQ14,
  input  DQ15
);

  wire nor_1_out;
  wire [15:0] rom_d;

  nor nor_1 (nor_1_out, nCE, nOE);
  ROM #(.AddrBits(19), .Bits(16)) rom (.D(rom_d));  // open: A, sel
  PowerSupply powersupply_1 (.VDD(VCC), .GND(GND));
  BusSplitter #(.Bits(16)) bussplitter_1 (
    .D(rom_d), .D0(DQ0), .D1(DQ1), .D2(DQ2), .D3(DQ3), .D4(DQ4), .D5(DQ5), .D6(DQ6), .D7(DQ7), .D8(DQ8),
    .D9(DQ9), .D10(DQ10), .D11(DQ11), .D12(DQ12), .D13(DQ13), .D14(DQ14), .D15(DQ15));  // open: OE

  // Notes on the sheet:
  //   nCE: pin 26, default 1
  //   nOE: pin 28, default 1
  //   A_1: pin 1
  //   A0: pin 48
  //   A1: pin 47
  //   A2: pin 46
  //   A3: pin 45
  //   A4: pin 44
  //   A5: pin 43
  //   A6: pin 42
  //   A7: pin 41
  //   A8: pin 40
  //   A9: pin 39
  //   A10: pin 6
  //   A11: pin 5
  //   A12: pin 4
  //   A13: pin 3
  //   A14: pin 2
  //   A15: pin 38
  //   A16: pin 37
  //   A17: pin 36
  //   A18: pin 35
  //   VCC: pin 25, default 1
  //   GND: pin 24
  //   DQ0: pin 29
  //   DQ1: pin 31
  //   DQ2: pin 33
  //   DQ3: pin 8
  //   DQ4: pin 10
  //   DQ5: pin 12
  //   DQ6: pin 14
  //   DQ7: pin 16
  //   DQ8: pin 18
  //   DQ9: pin 20
  //   DQ10: pin 22
  //   DQ11: pin 30
  //   DQ12: pin 32
  //   DQ13: pin 34
  //   DQ14: pin 7
  //   DQ15: pin 9
endmodule
