// Digital circuit neocart_cart.dig as structural Verilog
module neocart_cart (
  input  [18:0] A_19_1,
  input  nAS,
  input  ROMOEU,
  input  ROMOEL,
  input  nRW,
  input  _68KCLK,
  input  ROMOE,
  output [15:0] D_15_0,
  output PDTACK,
  output ROMWAIT
);

  wire and_1_out, not_1_out, not_2_out, not_3_out, not_4_out;

  not not_1 (not_1_out, nAS);
  not not_2 (not_2_out, ROMOEU);
  not not_3 (not_3_out, ROMOEL);
  not not_4 (not_4_out, nRW);
  and and_1 (and_1_out, not_1_out, not_2_out, not_4_out);  // open: In_4
  ROM #(.AddrBits(19), .Bits(16)) S29GL064_NOR_Flash (.A(A_19_1), .sel(and_1_out), .D(D_15_0));
  not not_5 (PDTACK, and_1_out);

  assign ROMWAIT = 1'b1;

  // Notes on the sheet:
  //   nAS: default 1
  //   ROMOEU: default 1
  //   ROMOEL: default 1
  //   nRW: default 1
  //   ROMOE: default 1
  //   contents of S29GL064_NOR_Flash (hex, n*v repeats v):
  //   10,f300,c0,402,c0,408,c0,40e,c0,414,0,186,0,186,0,186
endmodule
