// Digital circuit neocart_prom.dig as structural Verilog
// NeoCart PROG Slot — CPLD + NOR Flash
// Address decode + bankswitch register + ROM lookup.
// Inputs: ADDR[23:1], DATA_IN[15:0], AS_n, ROMOE_n, RW_n, CLK, RST_n
// Outputs: DATA_OUT[15:0], DTACK_n
// Memory map:
//   0x000000-0x0FFFFF : P1 fixed (1MB)
//   0x200000-0x2FFFFF : P2 banked (1MB window)
//   0x2FFFF0 write    : bankswitch register
module neocart_prom (
  input  [22:0] ADDR,
  input  [15:0] DATA_IN,
  input  AS_n,
  input  ROMOE_n,
  input  RW_n,
  input  CLK,
  input  RST_n,
  output [15:0] DATA_OUT,
  output DTACK_n
);

  wire and_1_out, and_2_out, and_3_out, not_1_out, not_2_out, not_3_out;
  wire [9:0] multiplexer_1_out;

  not not_1 (not_1_out, AS_n);
  not not_2 (not_2_out, ROMOE_n);
  not not_3 (not_3_out, RW_n);
  and and_1 (and_1_out, not_1_out, not_2_out, not_3_out);
  buf and_2 (and_2_out, not_1_out);  // And open: In_2
  Comparator #(.Bits(4)) comparator_1 (.a(ADDR[22:19]), .b(4'b0000));  // open: gt, eq, lt
  Comparator #(.Bits(4)) comparator_2 (.a(ADDR[22:19]), .b(4'b0010));  // open: gt, eq, lt
  Comparator #(.Bits(20)) comparator_3 (.a(ADDR[22:3]), .b(20'h2ffff));  // open: gt, eq, lt
  Multiplexer #(.Bits(10)) multiplexer_1 (.in_0(ADDR[9:0]), .out(multiplexer_1_out));  // open: sel, in_1
  buf and_3 (and_3_out, and_2_out);  // And open: In_2
  ROM #(.AddrBits(10), .Bits(16)) P_ROM (.sel(and_1_out), .D(DATA_OUT));  // open: A
  Register #(.Bits(3)) BANK_REG (.D(DATA_IN[2:0]), .C(CLK), .en(and_3_out));  // open: Q
  not not_4 (DTACK_n, and_1_out);
  // Pins of 3 and 16 bits meet at DATA_IN

  // Notes on the sheet:
  //   NeoCart PROG — CPLD + NOR Flash Cart Simulation
  //   Address decode → bankswitch register → ROM lookup → data output
  //   This is the circuit that would be synthesized into the EPM240 CPLD.
  //   The ROM block represents the NOR flash chip (S29GL064).
  //   contents of P_ROM (hex, n*v repeats v):
  //   0010,F300,00C0,0402,00C0,0408,00C0,040E,00C0,0414,0000,0186,0000,0186,0000,0186
endmodule
