// Digital circuit neocart_test.dig as structural Verilog
module neocart_test (
  input  [3:0] ADDR,
  input  CS,
  output [15:0] DATA
);

  ROM #(.AddrBits(4), .Bits(16)) NOR_FLASH (.A(ADDR), .sel(CS), .D(DATA));

  // Notes on the sheet:
  //   contents of NOR_FLASH (hex, n*v repeats v):
  //   10,f300,c0,402,c0,408,c0,40e,c0,414,0,186,0,186,0,186
endmodule

/* Test case ROM_Read:
ADDR CS DATA
0x0  1  0x0010
0x1  1  0xF300
0x2  1  0x00C0
0x3  1  0x0402
0x4  1  0x00C0
0x5  1  0x0408
0x0  0  X
*/
